// Logisim project FinalProject.circ as structural Verilog: 8 circuits, main circuit main
module main (
  input  [7:0] in_1,
  input  Manual_cycle,
  input  Reset
);

  wire bus_control_1_alu_enable, bus_control_1_ram_read, bus_control_1_ram_write,
       bus_control_1_register_write, button_1_out, Goto_enable, nand_1_out;
  wire [1:0] clock_1_state;
  wire [3:0] A, B, bus_control_1_opcode_to_alu, D, decoder_1_opcode, ram_data;
  wire [7:0] goto_imm, imm, Instruction, ram_address;
  wire [15:0] register_1_q, rom_1_data;
  wire [31:0] alu_1_output, n16_register_file_1_a, n16_register_file_1_b;

  decoder decoder_1 (
    .Input(register_1_q), .RegB(B), .RegA(A), .DestinationREG(D), .opcode(decoder_1_opcode),
    .RAM_Address(ram_address), .RAM_Data(ram_data), .GOTO_Address(goto_imm), .Imm_to_Reg(imm));
  Button button_1 (.out(button_1_out));
  Transistor #(.\type ("n"), .width(8)) transistor_1 (.in(in_1), .out(Instruction), .gate(button_1_out));
  nand nand_1 (nand_1_out, clock_1_state[0], clock_1_state[1]);
  ROM #(.dataWidth(16)) rom_1 (.addr(Instruction), .data(rom_1_data));  // open: sel
  Register #(.width(16)) register_1 (.D(rom_1_data), .Q(register_1_q), .clk(nand_1_out));  // open: en, clr
  _16_register_file u_16_register_file_1 (
    .d(alu_1_output), .Clk(bus_control_1_register_write), .Rd(D), .Clr(Reset), .Ra(A), .Rb(B),
    .a(n16_register_file_1_a), .b(n16_register_file_1_b));
  Clock clock_1 (
    .New_Value(goto_imm), .OpCode(decoder_1_opcode), .Manual_Cycle(Manual_cycle), .Reset(Reset),
    .Counter(Instruction), .State(clock_1_state));
  alu alu_1 (
    .A(n16_register_file_1_a), .B(n16_register_file_1_b), .imm(imm), .Op_code(bus_control_1_opcode_to_alu),
    .in_5(bus_control_1_alu_enable), .\output (alu_1_output));
  bus_control bus_control_1 (
    .Cycle_LSB(clock_1_state[0]), .Cycle_MSB(clock_1_state[1]), .OP(decoder_1_opcode),
    .ALU_Enable(bus_control_1_alu_enable), .Register_Write(bus_control_1_register_write),
    .RAM_Read(bus_control_1_ram_read), .RAM_Write(bus_control_1_ram_write),
    .OPCode_to_ALU(bus_control_1_opcode_to_alu), .Program_Counter_Update(Goto_enable));
  RAM #(.dataWidth(32), .bus("separate")) ram_1 (
    .addr(ram_address), .din(n16_register_file_1_a), .data(alu_1_output), .str(bus_control_1_ram_write),
    .clk(bus_control_1_ram_write), .ld(bus_control_1_ram_read), .clr(Reset));  // open: sel

  // Notes on the sheet:
  //   ROM (Instructions)
  //   contents of rom_1 (hex, n*v repeats v):
  //   f105 c100 b300 232 e000
  //   Clock
  //   Registers
  //   32-bit CPU
  //   By Cliff, Will, Tom, & Crissy
  //   ALU
  //   Bus Control
  //   RAM
endmodule

module _16_register_file (
  input  [31:0] d,
  input  Clk,
  input  [3:0] Rd,
  input  Clr,
  input  [3:0] Ra,
  input  [3:0] Rb,
  output [31:0] a,
  output [31:0] b
);

  wire demultiplexer_1_out0, demultiplexer_1_out1, demultiplexer_1_out2, demultiplexer_1_out3;
  wire [31:0] n3_register_file_1_a, n3_register_file_1_b, n4_register_file_1_a, n4_register_file_1_b,
       n4_register_file_2_a, n4_register_file_2_b, n4_register_file_3_a, n4_register_file_3_b;

  Demultiplexer #(.select(2), .enable("false")) demultiplexer_1 (
    .out0(demultiplexer_1_out0), .out1(demultiplexer_1_out1), .out2(demultiplexer_1_out2),
    .out3(demultiplexer_1_out3), .in(Clk), .sel(Rd[3:2]));
  _3_register_file u_3_register_file_1 (
    .d(d), .Ck(demultiplexer_1_out0), .Rd(Rd[1:0]), .Clr(Clr), .Ra(Ra[1:0]), .Rb(Rb[1:0]),
    .a(n3_register_file_1_a), .b(n3_register_file_1_b));
  _4_register_file u_4_register_file_1 (
    .d(d), .Ck(demultiplexer_1_out1), .Rd(Rd[1:0]), .Clr(Clr), .Ra(Ra[1:0]), .Rb(Rb[1:0]),
    .a(n4_register_file_1_a), .b(n4_register_file_1_b));
  _4_register_file u_4_register_file_2 (
    .d(d), .Ck(demultiplexer_1_out2), .Rd(Rd[1:0]), .Clr(Clr), .Ra(Ra[1:0]), .Rb(Rb[1:0]),
    .a(n4_register_file_2_a), .b(n4_register_file_2_b));
  _4_register_file u_4_register_file_3 (
    .d(d), .Ck(demultiplexer_1_out3), .Rd(Rd[1:0]), .Clr(Clr), .Ra(Ra[1:0]), .Rb(Rb[1:0]),
    .a(n4_register_file_3_a), .b(n4_register_file_3_b));
  Multiplexer #(.select(2), .width(32), .enable("false")) multiplexer_1 (
    .in0(n3_register_file_1_a), .in1(n4_register_file_1_a), .in2(n4_register_file_2_a),
    .in3(n4_register_file_3_a), .out(a), .sel(Ra[3:2]));
  Multiplexer #(.select(2), .width(32), .enable("false")) multiplexer_2 (
    .in0(n3_register_file_1_b), .in1(n4_register_file_1_b), .in2(n4_register_file_2_b),
    .in3(n4_register_file_3_b), .out(b), .sel(Rb[3:2]));

  // Notes on the sheet:
  //   Data in
  //   Write data to register
  //   Note the splitter
  //   Which register?
  //   Reset everything
  //   Select the contents of two registers, Ra Rb
  //   Value of two registers selected
endmodule

module _4_register_file (
  input  [31:0] d,
  input  Ck,
  input  [1:0] Rd,
  input  Clr,
  input  [1:0] Ra,
  input  [1:0] Rb,
  output [31:0] a,
  output [31:0] b
);

  wire demultiplexer_1_out0, demultiplexer_1_out1, demultiplexer_1_out2, demultiplexer_1_out3;
  wire [31:0] register_1_q, register_2_q, register_3_q, register_4_q;

  Demultiplexer #(.select(2), .enable("false")) demultiplexer_1 (
    .out0(demultiplexer_1_out0), .out1(demultiplexer_1_out1), .out2(demultiplexer_1_out2),
    .out3(demultiplexer_1_out3), .in(Ck), .sel(Rd));
  Register #(.width(32)) register_1 (.D(d), .Q(register_1_q), .clk(demultiplexer_1_out0), .clr(Clr));  // open: en
  Register #(.width(32)) register_2 (.D(d), .Q(register_2_q), .clk(demultiplexer_1_out1), .clr(Clr));  // open: en
  Register #(.width(32)) register_3 (.D(d), .Q(register_3_q), .clk(demultiplexer_1_out2), .clr(Clr));  // open: en
  Register #(.width(32)) register_4 (.D(d), .Q(register_4_q), .clk(demultiplexer_1_out3), .clr(Clr));  // open: en
  Multiplexer #(.select(2), .width(32), .enable("false")) multiplexer_1 (
    .in0(register_1_q), .in1(register_2_q), .in2(register_3_q), .in3(register_4_q), .out(a), .sel(Ra));
  Multiplexer #(.select(2), .width(32), .enable("false")) multiplexer_2 (
    .in0(register_1_q), .in1(register_2_q), .in2(register_3_q), .in3(register_4_q), .out(b), .sel(Rb));

  // Notes on the sheet:
  //   Data in
  //   Write signal
  //   Select register to write to
  //   Reset
  //   Registers to select to read from
  //   Values of selected registers
endmodule

module _3_register_file (
  input  [31:0] d,
  input  Ck,
  input  [1:0] Rd,
  input  Clr,
  input  [1:0] Ra,
  input  [1:0] Rb,
  output [31:0] a,
  output [31:0] b
);

  wire demultiplexer_1_out1, demultiplexer_1_out2, demultiplexer_1_out3;
  wire [31:0] register_1_q, register_2_q, register_3_q;

  Demultiplexer #(.select(2), .enable("false")) demultiplexer_1 (
    .out1(demultiplexer_1_out1), .out2(demultiplexer_1_out2), .out3(demultiplexer_1_out3), .in(Ck), .sel(Rd));  // open: out0
  Register #(.width(32)) register_1 (.D(d), .Q(register_1_q), .clk(demultiplexer_1_out1), .clr(Clr));  // open: en
  Register #(.width(32)) register_2 (.D(d), .Q(register_2_q), .clk(demultiplexer_1_out2), .clr(Clr));  // open: en
  Register #(.width(32)) register_3 (.D(d), .Q(register_3_q), .clk(demultiplexer_1_out3), .clr(Clr));  // open: en
  Multiplexer #(.select(2), .width(32), .enable("false")) multiplexer_1 (
    .in0({32{1'b0}}), .in1(register_1_q), .in2(register_2_q), .in3(register_3_q), .out(a), .sel(Ra));
  Multiplexer #(.select(2), .width(32), .enable("false")) multiplexer_2 (
    .in0({32{1'b0}}), .in1(register_1_q), .in2(register_2_q), .in3(register_3_q), .out(b), .sel(Rb));

  // Notes on the sheet:
  //   R0
  //   R1
  //   R2
  //   R3
endmodule

module bus_control (
  input  Cycle_LSB,
  input  Cycle_MSB,
  input  [3:0] OP,
  output ALU_Enable,
  output Register_Write,
  output RAM_Read,
  output RAM_Write,
  output [3:0] OPCode_to_ALU,
  output Program_Counter_Update
);

  wire [3:1] rom_1_data;

  Multiplexer #(.select(4), .width(4), .enable("false")) multiplexer_1 (
    .in0(OP), .in1(OP), .in2(OP), .in3(OP), .in4(OP), .in5(OP), .in6(OP), .in7(OP), .in8(OP), .in9(OP),
    .in12(4'b0000), .in13(4'b0000), .in14(4'b0101), .in15(OP), .out(OPCode_to_ALU), .sel(OP));  // open: in10, in11
  ROM #(.addrWidth(6)) rom_1 (
    .addr({OP, Cycle_MSB, Cycle_LSB}),
    .data({ALU_Enable, Register_Write, RAM_Read, RAM_Write, rom_1_data, Program_Counter_Update}));  // open: sel

  // Notes on the sheet:
  //   contents of rom_1 (hex, n*v repeats v):
  //   80 c0 0 0 80 c0 0 0 80 c0 0 0 80 c0 0 0 80 c0 0 0 80 c0 0 0 80 c0 0 0 80 c0 0 0 80 c0 0 0 80 c0 0 0
  //   20 60 0 0 20 60 0 0 80 90 0 0 80 90 0 0 80 81 0 0 80 c0
endmodule

module alu (
  input  [31:0] A,
  input  [31:0] B,
  input  [7:0] imm,
  input  [3:0] Op_code,
  input  in_5,
  output [31:0] \output 
);

  wire comparator_1_eq, comparator_1_gt, comparator_1_lt;
  wire [31:0] adder_1_out, and_1_out, bit_extender_1_out, bit_extender_2_out, bit_extender_3_out,
       bit_extender_4_out, divider_1_out, multiplexer_1_out, multiplier_1_out, or_1_out, subtractor_1_out,
       xnor_1_out;

  assign bit_extender_1_out = {{24{1'b0}}, imm};  // Bit_Extender bit_extender_1
  Adder #(.width(32)) adder_1 (.a(A), .b(B), .out(adder_1_out));  // open: cin, cout
  Subtractor #(.width(32)) subtractor_1 (.a(A), .b(B), .out(subtractor_1_out));  // open: bin, bout
  Multiplier #(.width(32)) multiplier_1 (.a(A), .b(B), .out(multiplier_1_out));  // open: cin, cout
  Divider #(.width(32)) divider_1 (.a(A), .b(B), .out(divider_1_out));  // open: upper, rem
  assign bit_extender_2_out = {{31{1'b0}}, comparator_1_gt};  // Bit_Extender bit_extender_2
  assign bit_extender_3_out = {{31{1'b0}}, comparator_1_eq};  // Bit_Extender bit_extender_3
  Comparator #(.width(32)) comparator_1 (
    .a(A), .b(B), .gt(comparator_1_gt), .eq(comparator_1_eq), .lt(comparator_1_lt));
  assign bit_extender_4_out = {{31{1'b0}}, comparator_1_lt};  // Bit_Extender bit_extender_4
  assign and_1_out = A & B;  // AND_Gate and_1, 32 bits wide
  assign or_1_out = A | B;  // OR_Gate or_1, 32 bits wide
  assign xnor_1_out = ~(A ^ B);  // XNOR_Gate xnor_1, 32 bits wide
  Multiplexer #(.select(4), .width(32), .enable("false")) multiplexer_1 (
    .in0(adder_1_out), .in1(subtractor_1_out), .in2(multiplier_1_out), .in3(divider_1_out),
    .in4(bit_extender_2_out), .in5(bit_extender_3_out), .in6(bit_extender_4_out), .in7(and_1_out),
    .in8(or_1_out), .in9(xnor_1_out), .in10(bit_extender_1_out), .in11(bit_extender_1_out),
    .in12(bit_extender_1_out), .in13(bit_extender_1_out), .in14(bit_extender_1_out),
    .in15(bit_extender_1_out), .out(multiplexer_1_out), .sel(Op_code));
  assign \output  = in_5 ? multiplexer_1_out : 32'bz;  // Controlled_Buffer controlled_buffer_1
endmodule

module decoder (
  input  [15:0] Input,
  output [3:0] RegB,
  output [3:0] RegA,
  output [3:0] DestinationREG,
  output [3:0] opcode,
  output [7:0] RAM_Address,
  output [3:0] RAM_Data,
  output [7:0] GOTO_Address,
  output [7:0] Imm_to_Reg
);

  wire EqualsA, EqualsB, EqualsC, EqualsD, EqualsE, EqualsF, lessthenA;

  Comparator #(.width(4), .mode("unsigned")) comparator_1 (
    .a(Input[15:12]), .b(4'b1010), .lt(lessthenA));  // open: gt, eq
  Comparator #(.width(4), .mode("unsigned")) comparator_2 (
    .a(Input[15:12]), .b(4'b1010), .eq(EqualsA));  // open: gt, lt
  Comparator #(.width(4), .mode("unsigned")) comparator_3 (
    .a(Input[15:12]), .b(4'b1011), .eq(EqualsB));  // open: gt, lt
  Comparator #(.width(4), .mode("unsigned")) comparator_4 (
    .a(Input[15:12]), .b(4'b1100), .eq(EqualsC));  // open: gt, lt
  Comparator #(.width(4), .mode("unsigned")) comparator_5 (
    .a(Input[15:12]), .b(4'b1101), .eq(EqualsD));  // open: gt, lt
  Comparator #(.width(4), .mode("unsigned")) comparator_6 (
    .a(Input[15:12]), .b(4'b1110), .eq(EqualsE));  // open: gt, lt
  Comparator #(.width(4), .mode("unsigned")) comparator_7 (
    .a(Input[15:12]), .b(4'b1111), .eq(EqualsF));  // open: gt, lt
  Transistor #(.\type ("n"), .gate("br"), .width(4)) transistor_1 (.in(Input[3:0]), .out(RegB), .gate(lessthenA));
  Transistor #(.\type ("n"), .gate("br"), .width(4)) transistor_2 (.in(Input[7:4]), .out(RegA), .gate(lessthenA));
  Transistor #(.\type ("n"), .gate("br"), .width(4)) transistor_3 (
    .in(Input[11:8]), .out(DestinationREG), .gate(lessthenA));
  Transistor #(.\type ("n"), .gate("br"), .width(4)) transistor_4 (
    .in(Input[3:0]), .out(RAM_Address[3:0]), .gate(EqualsA));
  Transistor #(.\type ("n"), .gate("br"), .width(4)) transistor_5 (
    .in(Input[7:4]), .out(RAM_Address[7:4]), .gate(EqualsA));
  Transistor #(.\type ("n"), .gate("br"), .width(4)) transistor_6 (
    .in(Input[11:8]), .out(DestinationREG), .gate(EqualsA));
  Transistor #(.\type ("n"), .gate("br"), .width(4)) transistor_7 (
    .in(Input[3:0]), .out(RAM_Address[3:0]), .gate(EqualsB));
  Transistor #(.\type ("n"), .gate("br"), .width(4)) transistor_8 (
    .in(Input[7:4]), .out(RAM_Address[7:4]), .gate(EqualsB));
  Transistor #(.\type ("n"), .gate("br"), .width(4)) transistor_9 (
    .in(Input[11:8]), .out(DestinationREG), .gate(EqualsB));
  Transistor #(.\type ("n"), .gate("br"), .width(4)) transistor_10 (
    .in(Input[3:0]), .out(RAM_Address[3:0]), .gate(EqualsC));
  Transistor #(.\type ("n"), .gate("br"), .width(4)) transistor_11 (
    .in(Input[7:4]), .out(RAM_Address[7:4]), .gate(EqualsC));
  Transistor #(.\type ("n"), .gate("br"), .width(4)) transistor_12 (.in(Input[11:8]), .out(RegA), .gate(EqualsC));
  Transistor #(.\type ("n"), .gate("br"), .width(4)) transistor_13 (
    .in(Input[3:0]), .out(RAM_Address[3:0]), .gate(EqualsD));
  Transistor #(.\type ("n"), .gate("br"), .width(4)) transistor_14 (
    .in(Input[7:4]), .out(RAM_Address[7:4]), .gate(EqualsD));
  Transistor #(.\type ("n"), .gate("br"), .width(4)) transistor_15 (.in(Input[11:8]), .out(RAM_Data), .gate(EqualsD));
  Transistor #(.\type ("n"), .gate("br"), .width(4)) transistor_16 (
    .in(Input[3:0]), .out(GOTO_Address[3:0]), .gate(EqualsE));
  Transistor #(.\type ("n"), .gate("br"), .width(4)) transistor_17 (
    .in(Input[7:4]), .out(GOTO_Address[7:4]), .gate(EqualsE));
  Transistor #(.\type ("n"), .gate("br"), .width(4)) transistor_18 (.in(Input[11:8]), .out(RegA), .gate(EqualsE));
  Transistor #(.\type ("n"), .gate("br"), .width(4)) transistor_19 (.in(4'b0000), .out(RegB), .gate(EqualsE));
  Transistor #(.\type ("n"), .gate("br"), .width(4)) transistor_20 (
    .in(Input[3:0]), .out(Imm_to_Reg[3:0]), .gate(EqualsF));
  Transistor #(.\type ("n"), .gate("br"), .width(4)) transistor_21 (
    .in(Input[7:4]), .out(Imm_to_Reg[7:4]), .gate(EqualsF));
  Transistor #(.\type ("n"), .gate("br"), .width(4)) transistor_22 (
    .in(Input[11:8]), .out(DestinationREG), .gate(EqualsF));

  assign opcode = Input[15:12];

  // Other names for the same wires on the sheet: A[3:0] = RegA; B[3:0] = RegB; DEST[3:0] = DestinationREG;
  //   n4[3:0] = Input[3:0]; n3[3:0] = Input[7:4]; n2[3:0] = Input[11:8]
endmodule

module Clock (
  input  [7:0] New_Value,
  input  [3:0] OpCode,
  input  Manual_Cycle,
  input  Reset,
  output [7:0] Counter,
  output [1:0] State
);

  wire and_1_out, Clock_out, comparator_1_eq, not_1_out;
  wire [7:0] adder_1_out, multiplexer_2_out, toMux;

  Comparator #(.width(4)) comparator_1 (.a(4'b1110), .b(OpCode), .eq(comparator_1_eq));  // open: gt, lt
  Clock_part Clock (.out(Clock_out));
  or or_1 (State[0], Clock_out, Manual_Cycle);
  not not_1 (not_1_out, State[0]);
  Multiplexer #(.width(8), .enable("false")) multiplexer_1 (
    .in0(toMux), .in1(New_Value), .out(Counter), .sel(comparator_1_eq));
  Multiplexer #(.width(8), .enable("false")) multiplexer_2 (
    .in0(adder_1_out), .in1(Counter), .out(multiplexer_2_out), .sel(comparator_1_eq));
  Register u_Counter (.D(multiplexer_2_out), .Q(toMux), .clk(and_1_out), .clr(Reset));  // open: en
  and and_1 (and_1_out, State[0], State[1]);
  T_Flip_Flop t_ff_1 (.clk(not_1_out), .T(1'b1), .Q(State[1]), .reset(Reset));  // open: Qn, preset, en
  Adder adder_1 (.a(8'h1), .b(toMux), .out(adder_1_out));  // open: cin, cout
endmodule
