// Logisim project TOM_ALU_10-30-15.circ as structural Verilog
module ALU (
  input  [31:0] A,
  input  [31:0] B,
  input  [7:0] imm,
  input  [3:0] Op_code,
  input  in_5,
  output [31:0] \output 
);

  wire comparator_1_eq, comparator_1_gt, comparator_1_lt;
  wire [31:0] adder_1_out, and_1_out, bit_extender_1_out, bit_extender_2_out, bit_extender_3_out,
       bit_extender_4_out, divider_1_out, multiplexer_1_out, multiplier_1_out, or_1_out, subtractor_1_out,
       xnor_1_out;

  assign bit_extender_1_out = {{24{1'b0}}, imm};  // Bit_Extender bit_extender_1
  Adder #(.width(32)) adder_1 (.a(A), .b(B), .out(adder_1_out));  // open: cin, cout
  Subtractor #(.width(32)) subtractor_1 (.a(A), .b(B), .out(subtractor_1_out));  // open: bin, bout
  Multiplier #(.width(32)) multiplier_1 (.a(A), .b(B), .out(multiplier_1_out));  // open: cin, cout
  Divider #(.width(32)) divider_1 (.a(A), .b(B), .out(divider_1_out));  // open: upper, rem
  assign bit_extender_2_out = {{31{1'b0}}, comparator_1_gt};  // Bit_Extender bit_extender_2
  assign bit_extender_3_out = {{31{1'b0}}, comparator_1_eq};  // Bit_Extender bit_extender_3
  Comparator #(.width(32)) comparator_1 (
    .a(A), .b(B), .gt(comparator_1_gt), .eq(comparator_1_eq), .lt(comparator_1_lt));
  assign bit_extender_4_out = {{31{1'b0}}, comparator_1_lt};  // Bit_Extender bit_extender_4
  assign and_1_out = A & B;  // AND_Gate and_1, 32 bits wide
  assign or_1_out = A | B;  // OR_Gate or_1, 32 bits wide
  assign xnor_1_out = ~(A ^ B);  // XNOR_Gate xnor_1, 32 bits wide
  Multiplexer #(.select(4), .width(32), .enable("false")) multiplexer_1 (
    .in0(adder_1_out), .in1(subtractor_1_out), .in2(multiplier_1_out), .in3(divider_1_out),
    .in4(bit_extender_2_out), .in5(bit_extender_3_out), .in6(bit_extender_4_out), .in7(and_1_out),
    .in8(or_1_out), .in9(xnor_1_out), .in10(bit_extender_1_out), .in11(bit_extender_1_out),
    .in12(bit_extender_1_out), .in13(bit_extender_1_out), .in14(bit_extender_1_out),
    .in15(bit_extender_1_out), .out(multiplexer_1_out), .sel(Op_code));
  assign \output  = in_5 ? multiplexer_1_out : 32'bz;  // Controlled_Buffer controlled_buffer_1
endmodule
