// Logisim project TOM_DECODER_11_12_15.circ as structural Verilog: 2 circuits, main circuit Main
module Main (
);

  Router router_1 ();  // open: Input, RegB, RegA, DestinationREG, RAM_Address, RAM_Data, GOTO_Address, Imm_to_Reg
endmodule

module Router (
  input  [15:0] Input,
  output [3:0] RegB,
  output [3:0] RegA,
  output [3:0] DestinationREG,
  output [7:0] RAM_Address,
  output [3:0] RAM_Data,
  output [7:0] GOTO_Address,
  output [7:0] Imm_to_Reg
);

  wire EqualsA, EqualsB, EqualsC, EqualsD, EqualsE, EqualsF, lessthenA;
  wire [3:0] transistor_7_out;

  Comparator #(.width(4), .mode("unsigned")) comparator_1 (
    .a(Input[15:12]), .b(4'b1010), .lt(lessthenA));  // open: gt, eq
  Comparator #(.width(4), .mode("unsigned")) comparator_2 (
    .a(Input[15:12]), .b(4'b1010), .eq(EqualsA));  // open: gt, lt
  Comparator #(.width(4), .mode("unsigned")) comparator_3 (
    .a(Input[15:12]), .b(4'b1011), .eq(EqualsB));  // open: gt, lt
  Comparator #(.width(4), .mode("unsigned")) comparator_4 (
    .a(Input[15:12]), .b(4'b1100), .eq(EqualsC));  // open: gt, lt
  Comparator #(.width(4), .mode("unsigned")) comparator_5 (
    .a(Input[15:12]), .b(4'b1101), .eq(EqualsD));  // open: gt, lt
  Comparator #(.width(4), .mode("unsigned")) comparator_6 (
    .a(Input[15:12]), .b(4'b1110), .eq(EqualsE));  // open: gt, lt
  Comparator #(.width(4), .mode("unsigned")) comparator_7 (
    .a(Input[15:12]), .b(4'b1111), .eq(EqualsF));  // open: gt, lt
  Transistor #(.\type ("n"), .gate("br"), .width(4)) transistor_1 (.in(Input[3:0]), .out(RegB), .gate(lessthenA));
  Transistor #(.\type ("n"), .gate("br"), .width(4)) transistor_2 (.in(Input[7:4]), .out(RegA), .gate(lessthenA));
  Transistor #(.\type ("n"), .gate("br"), .width(4)) transistor_3 (
    .in(Input[11:8]), .out(DestinationREG), .gate(lessthenA));
  Transistor #(.\type ("n"), .gate("br"), .width(4)) transistor_4 (
    .in(Input[3:0]), .out(RAM_Address[3:0]), .gate(EqualsA));
  Transistor #(.\type ("n"), .gate("br"), .width(4)) transistor_5 (
    .in(Input[7:4]), .out(RAM_Address[7:4]), .gate(EqualsA));
  Transistor #(.\type ("n"), .gate("br"), .width(4)) transistor_6 (
    .in(Input[11:8]), .out(DestinationREG), .gate(EqualsA));
  Transistor #(.\type ("n"), .gate("br"), .width(4)) transistor_7 (
    .in(Input[3:0]), .out(transistor_7_out), .gate(EqualsB));
  Transistor #(.\type ("n"), .gate("br"), .width(4)) transistor_8 (.in(Input[7:4]), .out(RegA), .gate(EqualsB));
  Transistor #(.\type ("n"), .gate("br"), .width(4)) transistor_9 (
    .in(Input[11:8]), .out(DestinationREG), .gate(EqualsB));
  Transistor #(.\type ("n"), .gate("br"), .width(4)) transistor_10 (
    .in(Input[3:0]), .out(RAM_Address[3:0]), .gate(EqualsC));
  Transistor #(.\type ("n"), .gate("br"), .width(4)) transistor_11 (
    .in(Input[7:4]), .out(RAM_Address[7:4]), .gate(EqualsC));
  Transistor #(.\type ("n"), .gate("br"), .width(4)) transistor_12 (.in(Input[11:8]), .out(RegA), .gate(EqualsC));
  Transistor #(.\type ("n"), .gate("br"), .width(4)) transistor_13 (
    .in(Input[3:0]), .out(RAM_Address[3:0]), .gate(EqualsD));
  Transistor #(.\type ("n"), .gate("br"), .width(4)) transistor_14 (
    .in(Input[7:4]), .out(RAM_Address[7:4]), .gate(EqualsD));
  Transistor #(.\type ("n"), .gate("br"), .width(4)) transistor_15 (.in(Input[11:8]), .out(RAM_Data), .gate(EqualsD));
  Transistor #(.\type ("n"), .gate("br"), .width(4)) transistor_16 (
    .in(Input[3:0]), .out(GOTO_Address[3:0]), .gate(EqualsE));
  Transistor #(.\type ("n"), .gate("br"), .width(4)) transistor_17 (
    .in(Input[7:4]), .out(GOTO_Address[7:4]), .gate(EqualsE));
  Transistor #(.\type ("n"), .gate("br"), .width(4)) transistor_18 (.in(Input[11:8]), .out(RegA), .gate(EqualsE));
  Transistor #(.\type ("n"), .gate("br"), .width(4)) transistor_19 (
    .in(Input[3:0]), .out(Imm_to_Reg[3:0]), .gate(EqualsF));
  Transistor #(.\type ("n"), .gate("br"), .width(4)) transistor_20 (
    .in(Input[7:4]), .out(Imm_to_Reg[7:4]), .gate(EqualsF));
  Transistor #(.\type ("n"), .gate("br"), .width(4)) transistor_21 (
    .in(Input[11:8]), .out(DestinationREG), .gate(EqualsF));
  // also tied to GND on the sheet: {transistor_7_out[0], transistor_7_out[1], transistor_7_out[2], transistor_7_out[3]}

  // Other names for the same wires on the sheet: A[3:0] = RegA; DEST[3:0] = DestinationREG; n4[3:0] = Input[3:0];
  //   n3[3:0] = Input[7:4]; n2[3:0] = Input[11:8]
endmodule
