// Logisim project TOM_REGISTERS_11_6_2015.circ as structural Verilog: 2 circuits, main circuit Main
module Registers (
  input  [31:0] Input,
  input  Write,
  input  [3:0] Destination_Register_of_input,
  input  Reset,
  input  [3:0] Select_Register_going_to_A,
  input  [3:0] Select_Register_going_to_B,
  output [31:0] Output_A,
  output [31:0] Output_B
);

  wire demultiplexer_1_out1, demultiplexer_1_out2, demultiplexer_1_out3, demultiplexer_1_out4,
       demultiplexer_1_out5, demultiplexer_1_out6, demultiplexer_1_out7, demultiplexer_1_out8,
       demultiplexer_1_out9, demultiplexer_1_out10, demultiplexer_1_out11, demultiplexer_1_out12,
       demultiplexer_1_out13, demultiplexer_1_out14, demultiplexer_1_out15;
  wire [31:0] _1_q, _2_q, _3_q, _4_q, _5_q, _6_q, _7_q, _8_q, _9_q, a_q, b_q, c_q, d_q, e_q, f_q;

  Demultiplexer #(.select(4), .enable("false")) demultiplexer_1 (
    .out1(demultiplexer_1_out1), .out2(demultiplexer_1_out2), .out3(demultiplexer_1_out3),
    .out4(demultiplexer_1_out4), .out5(demultiplexer_1_out5), .out6(demultiplexer_1_out6),
    .out7(demultiplexer_1_out7), .out8(demultiplexer_1_out8), .out9(demultiplexer_1_out9),
    .out10(demultiplexer_1_out10), .out11(demultiplexer_1_out11), .out12(demultiplexer_1_out12),
    .out13(demultiplexer_1_out13), .out14(demultiplexer_1_out14), .out15(demultiplexer_1_out15), .in(Write),
    .sel(Destination_Register_of_input));  // open: out0
  Multiplexer #(.select(4), .width(32), .enable("false")) multiplexer_1 (
    .in0({32{1'b0}}), .in1(_1_q), .in2(_2_q), .in3(_3_q), .in4(_4_q), .in5(_5_q), .in6(_6_q), .in7(_7_q),
    .in8(_8_q), .in9(_9_q), .in10(a_q), .in11(b_q), .in12(c_q), .in13(d_q), .in14(e_q), .in15(f_q),
    .out(Output_A), .sel(Select_Register_going_to_A));
  Register #(.width(32)) _4 (.D(Input), .Q(_4_q), .clk(demultiplexer_1_out4), .clr(Reset));  // open: en
  Register #(.width(32)) _8 (.D(Input), .Q(_8_q), .clk(demultiplexer_1_out8), .clr(Reset));  // open: en
  Register #(.width(32)) c (.D(Input), .Q(c_q), .clk(demultiplexer_1_out12), .clr(Reset));  // open: en
  Register #(.width(32)) _1 (.D(Input), .Q(_1_q), .clk(demultiplexer_1_out1), .clr(Reset));  // open: en
  Register #(.width(32)) _5 (.D(Input), .Q(_5_q), .clk(demultiplexer_1_out5), .clr(Reset));  // open: en
  Register #(.width(32)) _9 (.D(Input), .Q(_9_q), .clk(demultiplexer_1_out9), .clr(Reset));  // open: en
  Register #(.width(32)) d (.D(Input), .Q(d_q), .clk(demultiplexer_1_out13), .clr(Reset));  // open: en
  Multiplexer #(.select(4), .width(32), .enable("false")) multiplexer_2 (
    .in0({32{1'b0}}), .in1(_1_q), .in2(_2_q), .in3(_3_q), .in4(_4_q), .in5(_5_q), .in6(_6_q), .in7(_7_q),
    .in8(_8_q), .in9(_9_q), .in10(a_q), .in11(b_q), .in12(c_q), .in13(d_q), .in14(e_q), .in15(f_q),
    .out(Output_B), .sel(Select_Register_going_to_B));
  Register #(.width(32)) _2 (.D(Input), .Q(_2_q), .clk(demultiplexer_1_out2), .clr(Reset));  // open: en
  Register #(.width(32)) _6 (.D(Input), .Q(_6_q), .clk(demultiplexer_1_out6), .clr(Reset));  // open: en
  Register #(.width(32)) a (.D(Input), .Q(a_q), .clk(demultiplexer_1_out10), .clr(Reset));  // open: en
  Register #(.width(32)) e (.D(Input), .Q(e_q), .clk(demultiplexer_1_out14), .clr(Reset));  // open: en
  Register #(.width(32)) _3 (.D(Input), .Q(_3_q), .clk(demultiplexer_1_out3), .clr(Reset));  // open: en
  Register #(.width(32)) _7 (.D(Input), .Q(_7_q), .clk(demultiplexer_1_out7), .clr(Reset));  // open: en
  Register #(.width(32)) b (.D(Input), .Q(b_q), .clk(demultiplexer_1_out11), .clr(Reset));  // open: en
  Register #(.width(32)) f (.D(Input), .Q(f_q), .clk(demultiplexer_1_out15), .clr(Reset));  // open: en
endmodule

module Main (
);

  Registers registers_1 ();  // open: Input, Write, Destination_Register_of_input, Reset, Select_Register_going_to_A, Output_A, Select_Register_going_to_B, Output_B
endmodule
