// Logisim project Decoder.circ as structural Verilog: 2 circuits, main circuit Main
module Decoder (
  input  [15:0] Input,
  output [3:0] RegA,
  output [3:0] RegB,
  output [3:0] Destination_register,
  output [3:0] opcode,
  output [3:0] Imm1,
  output [3:0] Imm2,
  output [3:0] GoTo_Imm
);

  wire [7:4] multiplexer_3_out;
  wire [11:0] demultiplexer_1_out0, demultiplexer_1_out1, demultiplexer_1_out2, demultiplexer_1_out3,
       demultiplexer_1_out4, demultiplexer_1_out5, demultiplexer_1_out6, demultiplexer_1_out7,
       demultiplexer_1_out8, demultiplexer_1_out9, demultiplexer_1_out10, demultiplexer_1_out11,
       demultiplexer_1_out12, demultiplexer_1_out13, demultiplexer_1_out14;

  Demultiplexer #(.select(4), .width(12), .enable("false")) demultiplexer_1 (
    .out0(demultiplexer_1_out0), .out1(demultiplexer_1_out1), .out2(demultiplexer_1_out2),
    .out3(demultiplexer_1_out3), .out4(demultiplexer_1_out4), .out5(demultiplexer_1_out5),
    .out6(demultiplexer_1_out6), .out7(demultiplexer_1_out7), .out8(demultiplexer_1_out8),
    .out9(demultiplexer_1_out9), .out10(demultiplexer_1_out10), .out11(demultiplexer_1_out11),
    .out12(demultiplexer_1_out12), .out13(demultiplexer_1_out13), .out14(demultiplexer_1_out14),
    .in(Input[11:0]), .sel(Input[15:12]));  // open: out15
  Multiplexer #(.select(4), .width(12), .enable("false")) multiplexer_1 (
    .in0(demultiplexer_1_out0), .in1(demultiplexer_1_out1), .in2(demultiplexer_1_out2),
    .in3(demultiplexer_1_out3), .in4(demultiplexer_1_out4), .in5(demultiplexer_1_out5),
    .in6(demultiplexer_1_out6), .in7(demultiplexer_1_out7), .in8(demultiplexer_1_out8),
    .in9(demultiplexer_1_out9), .out({Destination_register, RegB, RegA}), .sel(Input[15:12]));  // open: in10, in11, in12, in13, in14, in15
  Multiplexer #(.select(4), .width(12), .enable("false")) multiplexer_2 (
    .in10(demultiplexer_1_out10), .in12(demultiplexer_1_out12), .out({Destination_register, Imm2, Imm1}),
    .sel(Input[15:12]));  // open: in0, in1, in2, in3, in4, in5, in6, in7, in8, in9, in11, in13, in14, in15
  Multiplexer #(.select(4), .width(12), .enable("false")) multiplexer_3 (
    .in11(demultiplexer_1_out11), .out({Destination_register, multiplexer_3_out, RegA}), .sel(Input[15:12]));  // open: in0, in1, in2, in3, in4, in5, in6, in7, in8, in9, in10, in12, in13, in14, in15
  Multiplexer #(.select(4), .width(12), .enable("false")) multiplexer_4 (
    .in13(demultiplexer_1_out13), .out({RegA, GoTo_Imm, Imm1}), .sel(Input[15:12]));  // open: in0, in1, in2, in3, in4, in5, in6, in7, in8, in9, in10, in11, in12, in14, in15
  Multiplexer #(.select(4), .width(12), .enable("false")) multiplexer_5 (
    .in14(demultiplexer_1_out14), .out({RegA, GoTo_Imm, RegB}), .sel(Input[15:12]));  // open: in0, in1, in2, in3, in4, in5, in6, in7, in8, in9, in10, in11, in12, in13, in15

  assign opcode = Input[15:12];

  // Other names for the same wires on the sheet: B[3:0] = RegB
endmodule

module Main (
);

  Decoder decoder_1 ();  // open: Input, Destination_register, opcode, RegB, RegA, Imm1, Imm2, GoTo_Imm
endmodule
