// Logisim project Clock.circ as structural Verilog: 2 circuits, main circuit Test
module main (
  input  [7:0] Increment_by,
  input  [3:0] OpCode,
  input  Manual_Cycle,
  input  Reset,
  output [7:0] Counter,
  output [1:0] State
);

  wire and_1_out, Clock_out, comparator_1_eq, comparator_2_gt, not_1_out;
  wire [7:0] adder_1_out, multiplexer_1_out, or_1_out, toMux;

  Multiplexer #(.width(8), .enable("false")) multiplexer_1 (
    .in0({8{1'b0}}), .in1(Increment_by), .out(multiplexer_1_out), .sel(comparator_1_eq));
  Comparator #(.width(4)) comparator_1 (.a(4'b1110), .b(OpCode), .eq(comparator_1_eq));  // open: gt, lt
  Clock Clock (.out(Clock_out));
  assign or_1_out = {8{1'b0}} | multiplexer_1_out;  // OR_Gate or_1, 8 bits wide
  or or_2 (State[0], Clock_out, Manual_Cycle);
  not not_1 (not_1_out, State[0]);
  Multiplexer #(.width(8), .enable("false")) multiplexer_2 (
    .in0(toMux), .in1(or_1_out), .out(Counter), .sel(comparator_2_gt));
  Comparator comparator_2 (.a(or_1_out), .b({8{1'b0}}), .gt(comparator_2_gt));  // open: eq, lt
  Register u_Counter (.D(adder_1_out), .Q(toMux), .clk(and_1_out), .clr(Reset));  // open: en
  and and_1 (and_1_out, State[0], State[1]);
  T_Flip_Flop t_ff_1 (.clk(not_1_out), .T(1'b1), .Q(State[1]), .reset(Reset));  // open: Qn, preset, en
  Adder adder_1 (.a(8'h1), .b(toMux), .out(adder_1_out));  // open: cin, cout
endmodule

module Test (
  input  [7:0] increment_by,
  input  in_2,
  input  in_3,
  output [7:0] Counter,
  output [1:0] state
);

  // main Clock: pin names not known; wires that end beside it: increment_by, in_2, in_3, Counter, state
  Hex_Digit_Display hex_digit_display_1 (.value(Counter[7:4]));  // open: dp
  Hex_Digit_Display hex_digit_display_2 (.value(Counter[3:0]));  // open: dp
endmodule
