// Logisim project Toy.circ as structural Verilog: 1 circuit, main circuit main
module main (
  input  [3:0] in_1,
  input  in_2,
  input  [6:0] in_3,
  input  [6:0] in_4,
  input  [6:0] in_5,
  input  [6:0] in_6,
  input  [6:0] in_7,
  output [3:0] out_8,
  output [3:0] out_9
);

  Hex_Digit_Display hex_digit_display_1 (.value(in_1), .dp(in_2));
  Joystick joystick_1 (.x(out_8), .y(out_9));
  DotMatrix dotmatrix_1 (.col0(in_3), .col1(in_5), .col2(in_7), .col3(in_6), .col4(in_4));
  Clock clock_1 ();  // open: out
endmodule
