// Logisim project clock.circ as structural Verilog: 1 circuit, main circuit main
module main (
  input  in_1,
  input  in_2,
  input  [3:0] in_3,
  input  Reset
);

  wire and_1_out, and_2_out, clock_2_out, not_1_out, not_2_out, t_ff_1_qn, t_ff_2_q;
  wire [1:0] clock_1_out;
  wire [7:0] adder_1_out, adder_2_out, Counter_q, register_1_q;

  Clock clock_1 (.out(clock_1_out[0]));
  Hex_Digit_Display hex_digit_display_1 (.value(in_3));  // open: dp
  not not_1 (not_1_out, clock_1_out[0]);
  T_Flip_Flop t_ff_1 (.clk(not_1_out), .T(1'b1), .Q(clock_1_out[1]), .Qn(t_ff_1_qn));  // open: preset, reset, en
  Clock clock_2 (.out(clock_2_out));
  not not_2 (not_2_out, clock_2_out);
  Hex_Digit_Display hex_digit_display_2 (.value({in_2, in_1, clock_1_out}));  // open: dp
  and and_1 (and_1_out, clock_1_out[0], clock_1_out[1]);
  and and_2 (and_2_out, clock_2_out, t_ff_2_q);
  T_Flip_Flop t_ff_2 (.clk(not_2_out), .T(1'b1), .Q(t_ff_2_q), .reset(Reset));  // open: Qn, preset, en
  Adder adder_1 (.a(8'h1), .b(register_1_q), .out(adder_1_out));  // open: cin, cout
  Register register_1 (.D(adder_1_out), .Q(register_1_q), .clk(and_1_out));  // open: en, clr
  Adder adder_2 (.a(8'h1), .b(Counter_q), .out(adder_2_out));  // open: cin, cout
  Register Counter (.D(adder_2_out), .Q(Counter_q), .clk(and_2_out), .clr(Reset));  // open: en
endmodule
