// Logisim project cliff_bus_control_11-05-15.circ as structural Verilog: 1 circuit, main circuit main
module main (
  input  Cycle_MSB,
  input  Cycle_LSB,
  input  [3:0] OP,
  input  [3:0] Destination,
  input  [3:0] A,
  input  [3:0] B
);
endmodule
