// Logisim project cliff_bus_control_11-07-15.circ as structural Verilog: 1 circuit, main circuit main
module main (
  input  Cycle_LSB,
  input  Cycle_MSB,
  input  [3:0] OP,
  output ALU_Enable,
  output Register_Write,
  output RAM_Read,
  output RAM_Write,
  output [3:0] OPCode_to_ALU,
  output Program_Counter_Update
);

  wire [3:1] rom_1_data;

  Multiplexer #(.select(4), .width(4), .enable("false")) multiplexer_1 (
    .in0(OP), .in1(OP), .in2(OP), .in3(OP), .in4(OP), .in5(OP), .in6(OP), .in7(OP), .in8(OP), .in9(OP),
    .in12(4'b0000), .in13(4'b0000), .in14(4'b0101), .in15(4'b0101), .out(OPCode_to_ALU), .sel(OP));  // open: in10, in11
  ROM #(.addrWidth(6)) rom_1 (
    .addr({OP, Cycle_MSB, Cycle_LSB}),
    .data({ALU_Enable, Register_Write, RAM_Read, RAM_Write, rom_1_data, Program_Counter_Update}));  // open: sel

  // Notes on the sheet:
  //   contents of rom_1 (hex, n*v repeats v):
  //   80 c0 0 0 80 c0 0 0 80 c0 0 0 80 c0 0 0 80 c0 0 0 80 c0 0 0 80 c0 0 0 80 c0 0 0 80 c0 0 0 80 c0 0 0
  //   20 60 0 0 20 60 0 0 80 90 0 0 80 90 0 0 80 81 0 0 80 81
endmodule
