// Logisim project register-file.circ as structural Verilog
module three_register_file (
  input  [31:0] d,
  input  Ck,
  input  [1:0] Rd,
  input  Clr,
  input  [1:0] Ra,
  input  [1:0] Rb,
  output [31:0] a,
  output [31:0] b
);

  wire demultiplexer_1_out1, demultiplexer_1_out2, demultiplexer_1_out3;
  wire [31:0] register_1_q, register_2_q, register_3_q;

  Demultiplexer #(.select(2), .enable("false")) demultiplexer_1 (
    .out1(demultiplexer_1_out1), .out2(demultiplexer_1_out2), .out3(demultiplexer_1_out3), .in(Ck), .sel(Rd));  // open: out0
  Register #(.width(32)) register_1 (.D(d), .Q(register_1_q), .clk(demultiplexer_1_out1), .clr(Clr));  // open: en
  Register #(.width(32)) register_2 (.D(d), .Q(register_2_q), .clk(demultiplexer_1_out2), .clr(Clr));  // open: en
  Register #(.width(32)) register_3 (.D(d), .Q(register_3_q), .clk(demultiplexer_1_out3), .clr(Clr));  // open: en
  Multiplexer #(.select(2), .width(32), .enable("false")) multiplexer_1 (
    .in0({32{1'b0}}), .in1(register_1_q), .in2(register_2_q), .in3(register_3_q), .out(a), .sel(Ra));
  Multiplexer #(.select(2), .width(32), .enable("false")) multiplexer_2 (
    .in0({32{1'b0}}), .in1(register_1_q), .in2(register_2_q), .in3(register_3_q), .out(b), .sel(Rb));

  // Notes on the sheet:
  //   R0
  //   R1
  //   R2
  //   R3
endmodule

module four_register_file (
  input  [31:0] d,
  input  Ck,
  input  [1:0] Rd,
  input  Clr,
  input  [1:0] Ra,
  input  [1:0] Rb,
  output [31:0] a,
  output [31:0] b
);

  wire demultiplexer_1_out0, demultiplexer_1_out1, demultiplexer_1_out2, demultiplexer_1_out3;
  wire [31:0] register_1_q, register_2_q, register_3_q, register_4_q;

  Demultiplexer #(.select(2), .enable("false")) demultiplexer_1 (
    .out0(demultiplexer_1_out0), .out1(demultiplexer_1_out1), .out2(demultiplexer_1_out2),
    .out3(demultiplexer_1_out3), .in(Ck), .sel(Rd));
  Register #(.width(32)) register_1 (.D(d), .Q(register_1_q), .clk(demultiplexer_1_out0), .clr(Clr));  // open: en
  Register #(.width(32)) register_2 (.D(d), .Q(register_2_q), .clk(demultiplexer_1_out1), .clr(Clr));  // open: en
  Register #(.width(32)) register_3 (.D(d), .Q(register_3_q), .clk(demultiplexer_1_out2), .clr(Clr));  // open: en
  Register #(.width(32)) register_4 (.D(d), .Q(register_4_q), .clk(demultiplexer_1_out3), .clr(Clr));  // open: en
  Multiplexer #(.select(2), .width(32), .enable("false")) multiplexer_1 (
    .in0(register_1_q), .in1(register_2_q), .in2(register_3_q), .in3(register_4_q), .out(a), .sel(Ra));
  Multiplexer #(.select(2), .width(32), .enable("false")) multiplexer_2 (
    .in0(register_1_q), .in1(register_2_q), .in2(register_3_q), .in3(register_4_q), .out(b), .sel(Rb));

  // Notes on the sheet:
  //   Data in
  //   Write signal
  //   Select register to write to
  //   Reset
  //   Values of selected registers
  //   Registers to select to read from
endmodule

module _16_register_file (
  input  [31:0] d,
  input  Clk,
  input  [3:0] Rd,
  input  Clr,
  input  [3:0] Ra,
  input  [3:0] Rb,
  output [31:0] a,
  output [31:0] b
);

  wire demultiplexer_1_out0, demultiplexer_1_out1, demultiplexer_1_out2, demultiplexer_1_out3;
  wire [31:0] R0_R3_a, R0_R3_b, R4_R7_a, R4_R7_b, R8_Rb_a, R8_Rb_b, Rc_Rf_a, Rc_Rf_b;

  Demultiplexer #(.select(2), .enable("false")) demultiplexer_1 (
    .out0(demultiplexer_1_out0), .out1(demultiplexer_1_out1), .out2(demultiplexer_1_out2),
    .out3(demultiplexer_1_out3), .in(Clk), .sel(Rd[3:2]));
  three_register_file R0_R3 (
    .d(d), .Ck(demultiplexer_1_out0), .Rd(Rd[1:0]), .Clr(Clr), .Ra(Ra[1:0]), .Rb(Rb[1:0]), .a(R0_R3_a),
    .b(R0_R3_b));
  four_register_file R4_R7 (
    .d(d), .Ck(demultiplexer_1_out1), .Rd(Rd[1:0]), .Clr(Clr), .Ra(Ra[1:0]), .Rb(Rb[1:0]), .a(R4_R7_a),
    .b(R4_R7_b));
  four_register_file R8_Rb (
    .d(d), .Ck(demultiplexer_1_out2), .Rd(Rd[1:0]), .Clr(Clr), .Ra(Ra[1:0]), .Rb(Rb[1:0]), .a(R8_Rb_a),
    .b(R8_Rb_b));
  four_register_file Rc_Rf (
    .d(d), .Ck(demultiplexer_1_out3), .Rd(Rd[1:0]), .Clr(Clr), .Ra(Ra[1:0]), .Rb(Rb[1:0]), .a(Rc_Rf_a),
    .b(Rc_Rf_b));
  Multiplexer #(.select(2), .width(32), .enable("false")) multiplexer_1 (
    .in0(R0_R3_a), .in1(R4_R7_a), .in2(R8_Rb_a), .in3(Rc_Rf_a), .out(a), .sel(Ra[3:2]));
  Multiplexer #(.select(2), .width(32), .enable("false")) multiplexer_2 (
    .in0(R0_R3_b), .in1(R4_R7_b), .in2(R8_Rb_b), .in3(Rc_Rf_b), .out(b), .sel(Rb[3:2]));

  // Notes on the sheet:
  //   Data in
  //   Write data to register
  //   Note the splitter
  //   Which register?
  //   Reset everything
  //   Select the contents of two registers, Ra Rb
  //   Value of two registers selected
endmodule
